# Fritzing sketch MSF60 for V3 Module Carrier HAT plus OLED pin 32 (GPIO 12) (saved by Fritzing 0.9.8b)
circuit board: 6.49621cm x 3.58589cm
breadboards: 1

parts:
  PI = Raspberry Pi Zero
  OUT_/_INV = female pin header, 3 pins [form="♀ (female)"]
  OFF_/_AGC = female pin header, 3 pins [form="♀ (female)"]
  OLED_SSD1306 = OLED 128x64 I2C Monochrome Display GND-VDD
  OFF = Pushbutton [package=THT]
  AM_RECEIVER_V3 = female pin header, 6 pins [form="♀ (female)"]
  PDN_/_FLOAT = female pin header, 3 pins [form="♀ (female)"]

nets:
  N1: PI.pin_1, PI.pin_17, OLED_SSD1306.VDD
  N2: PI.pin_2, AM_RECEIVER_V3.pin1
  N3: PI.pin_3, OLED_SSD1306.SDA
  N4: PI.pin_5, OLED_SSD1306.SCK
  N5: PI.pin_6, PI.pin_9, PI.pin_25, PI.pin_34, PI.pin_39, OFF_/_AGC.pin2, OLED_SSD1306.GND, OFF.leg0, AM_RECEIVER_V3.pin6, PDN_/_FLOAT.pin1
  N6: PI.pin_32, OUT_/_INV.pin2
  N7: PI.pin_40, OFF.leg1
  N8: OUT_/_INV.pin1, AM_RECEIVER_V3.pin5
  N9: OUT_/_INV.pin3, AM_RECEIVER_V3.pin4
  N10: OFF_/_AGC.pin3, AM_RECEIVER_V3.pin2
  N11: AM_RECEIVER_V3.pin3, PDN_/_FLOAT.pin2

notes:
  1
  2
  39
  40
  github.com/GOTO-GOSUB

custom parts:
  OLED 128x64 I2C Monochrome Display GND-VDD: OLED 128x64 I2C Monochrome Display. Note: there are two variants of this part, this one is the GND VDD SCK SDA variant. The other is VDD GND SCK SDA. Make sure you select the part that matches your module as using the incorrect part will probably destroy your module! In addition the mounting holes are marked on silkscreen but not by default drilled. If you want drilled mounting holes, copy a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
