# Fritzing sketch MSF60 for V3 Module Carrier HAT pin 32 (GPIO 12) (saved by Fritzing 0.9.8b)
circuit board: 6.48255cm x 2.97561cm
breadboards: 1

parts:
  OUT_/_INV = female pin header, 3 pins [form="♀ (female)"]
  AGC_/_OFF = female pin header, 3 pins [form="♀ (female)"]
  PDN_/_FLOAT = female pin header, 3 pins [form="♀ (female)"]
  ANT = Screw terminal - 2 pins [package=THT]
  ANT_2 = female pin header, 2 pins [form="♀ (female)"]
  UNIVERSAL_SOLDER = female pin header, 6 pins [form="♀ (female)"]
  3_3V_/_5V = female pin header, 3 pins [form="♀ (female)"]
  PI = Raspberry Pi Zero

nets:
  N1: OUT_/_INV.pin1, UNIVERSAL_SOLDER.pin5
  N2: OUT_/_INV.pin2, PI.pin_32
  N3: OUT_/_INV.pin3, UNIVERSAL_SOLDER.pin4
  N4: AGC_/_OFF.pin1, UNIVERSAL_SOLDER.pin2
  N5: AGC_/_OFF.pin2, PDN_/_FLOAT.pin1, UNIVERSAL_SOLDER.pin6, PI.pin_9, PI.pin_25, PI.pin_39
  N6: PDN_/_FLOAT.pin2, UNIVERSAL_SOLDER.pin3
  N7: ANT.pin1, ANT_2.pin1
  N8: ANT.pin2, ANT_2.pin2
  N9: UNIVERSAL_SOLDER.pin1, 3_3V_/_5V.pin2
  N10: 3_3V_/_5V.pin1, PI.pin_1, PI.pin_17
  N11: 3_3V_/_5V.pin3, PI.pin_2, PI.pin_4

notes:
  1
  2
  39
  40
  github.com/GOTO-GOSUB
  ATOMIC CLOCK Rx V3
  3-15V
  AON
  PDN
  OUT+
  OUT-
  GND
  v1.0
